// Logisim project s-mips.circ as structural Verilog: 16 circuits, main circuit S-MIPS Board
module S_MIPS_Board (
  input  DESHABILITAR_DISPATCHER,
  output halt
);

  wire button_1_out, CLK, CS, d_ff_1_q, LCLR, LoadRAM, LoadRAMOn, LW, R_R_W, R_W, ram_dispatcher_1_finished,
       RCS, Reset_out, RST, TTY_EN;
  wire [2:0] KDB;
  wire [3:0] LMask, Mask, ram_1_read_time, ram_1_write_time, RMask;
  wire [6:0] KDB_DATA, TTY_DATA;
  wire [15:0] Addr, LAddr, RAddr;
  wire [31:0] I0, I1, I2, I3, LData, ram_1_data_out_0, ram_1_data_out_1, ram_1_data_out_2, ram_1_data_out_3,
       RI0, RI1, RI2, RI3;

  TTY #(.rows(25), .cols(80)) tty_1 (.data(TTY_DATA), .clk(CLK), .we(TTY_EN), .clr(RST));
  not not_1 (LoadRAMOn, ram_dispatcher_1_finished);
  RAM_Dispatcher ram_dispatcher_1 (
    .WriteTime(ram_1_write_time), .Clock(CLK), .Data(LData), .Address(LAddr), .Mask(LMask),
    .Finished(ram_dispatcher_1_finished), .Write(LW), .CLR(LCLR));
  Keyboard #(.buflen(64)) keyboard_1 (.clk(CLK), .re(KDB[0]), .avail(KDB[2]), .data(KDB_DATA));  // open: clr
  RAM ram_1 (
    .Address(RAddr), .Data_Out_0(ram_1_data_out_0), .Data_Out_1(ram_1_data_out_1),
    .Data_Out_2(ram_1_data_out_2), .Data_Out_3(ram_1_data_out_3), .Data_In_0(RI0), .Data_In_1(RI1),
    .Data_In_2(RI2), .Data_In_3(RI3), .Mask(RMask), .nRead_Write(R_R_W), .Chip_Select(RCS),
    .Read_Time(ram_1_read_time), .Reset(button_1_out), .Write_Time(ram_1_write_time));
  Button button_1 (.out(button_1_out));
  D_Flip_Flop d_ff_1 (.clk(CLK), .D(1'b1), .Q(d_ff_1_q), .reset(Reset_out));  // open: Qn, preset, en
  Button Reset (.out(Reset_out));
  S_MIPS s_mips_1 (
    .Kbd_Enable(KDB[0]), .Address(Addr), .Kbd_Clear(KDB[1]), .Kbd_Available(KDB[2]), .RAM_In_0(I0),
    .Kbd_ASCII_Data(KDB_DATA), .RAM_In_1(I1), .TTY_Enable(TTY_EN), .RAM_In_2(I2), .RAM_In_3(I2),
    .TTY_ASCII_Data(TTY_DATA), .Reset(RST), .RAM_Out_0(ram_1_data_out_0), .Clock(CLK),
    .RAM_Out_1(ram_1_data_out_1), .Stop(halt), .RAM_Out_2(ram_1_data_out_2), .RAM_Out_3(ram_1_data_out_3),
    .Mask(Mask), .Read_Time(ram_1_read_time), .Write_Time(ram_1_write_time), .nRead_Write(R_W),
    .Chip_Select(CS));
  D_Flip_Flop d_ff_2 (.clk(CLK), .D(d_ff_1_q), .Qn(LCLR), .reset(Reset_out));  // open: Q, preset, en
  or or_1 (RST, LCLR, LoadRAM);
  Clock clock_1 (.out(CLK));
  Multiplexer #(.width(32), .enable("false")) multiplexer_1 (.in0(I0), .in1(LData), .out(RI0), .sel(LoadRAM));
  Multiplexer #(.width(32), .enable("false")) multiplexer_2 (.in0(I1), .in1(LData), .out(RI1), .sel(LoadRAM));
  Multiplexer #(.width(32), .enable("false")) multiplexer_3 (.in0(I2), .in1(LData), .out(RI2), .sel(LoadRAM));
  Multiplexer #(.width(32), .enable("false")) multiplexer_4 (.in0(I3), .in1(LData), .out(RI3), .sel(LoadRAM));
  and and_1 (LoadRAM, ~DESHABILITAR_DISPATCHER, LoadRAMOn);  // AND_Gate
  Multiplexer #(.width(16), .enable("false")) multiplexer_5 (.in0(Addr), .in1(LAddr), .out(RAddr), .sel(LoadRAM));
  Multiplexer #(.width(4), .enable("false")) multiplexer_6 (.in0(Mask), .in1(LMask), .out(RMask), .sel(LoadRAM));
  Multiplexer #(.enable("false")) multiplexer_7 (.in0(CS), .in1(LW), .out(RCS), .sel(LoadRAM));
  Multiplexer #(.enable("false")) multiplexer_8 (.in0(R_W), .in1(LW), .out(R_R_W), .sel(LoadRAM));

  // Notes on the sheet:
  //   NO MODIFICAR
  //   Keyboard
endmodule

module RAM (
  input  [15:0] Address,
  input  [31:0] Data_In_0,
  input  [31:0] Data_In_1,
  input  [31:0] Data_In_2,
  input  [31:0] Data_In_3,
  input  [3:0] Mask,
  input  nRead_Write,
  input  Chip_Select,
  input  Reset,
  output [31:0] Data_Out_0,
  output [31:0] Data_Out_1,
  output [31:0] Data_Out_2,
  output [31:0] Data_Out_3,
  output [3:0] Read_Time,
  output [3:0] Write_Time
);

  wire and_2_out, and_3_out, and_4_out, and_5_out, and_6_out, and_7_out, and_8_out, and_9_out, Changed, CLK,
       comparator_2_eq, comparator_3_eq, comparator_4_eq, comparator_5_eq, comparator_6_eq, Count,
       demultiplexer_3_out0, Idle, Idle_q, Load, Load0, Load1, nand_1_out, or_1_out, or_2_out, or_3_out,
       or_4_out, or_5_out, or_6_out, or_7_out, or_8_out, or_9_out, or_10_out, Proc_q, Update_Mem, Zero_Time;
  wire [3:0] counter_1_q, multiplexer_1_out, subtractor_1_out;
  wire [31:0] register_1_q, register_2_q, register_3_q, register_4_q, register_5_q;

  // Probe on 4'b0011
  // Probe on 4'b0010
  Multiplexer #(.width(4), .enable("false")) multiplexer_1 (
    .in0(4'b0011), .in1(4'b0010), .out(multiplexer_1_out), .sel(nRead_Write));
  or or_1 (or_1_out, Idle, Update_Mem);
  or or_2 (or_2_out, ~Chip_Select, Reset);  // OR_Gate
  Subtractor #(.width(4)) subtractor_1 (.a(multiplexer_1_out), .b(4'b0010), .out(subtractor_1_out));  // open: bin, bout
  D_Flip_Flop u_Idle (.clk(CLK), .D(or_1_out), .Q(Idle_q), .preset(or_2_out));  // open: Qn, en, reset
  Demultiplexer #(.enable("false")) demultiplexer_1 (.out0(Idle), .out1(Load0), .in(Idle_q), .sel(Changed));
  // Probe on counter_1_q
  Counter #(.width(4), .max('hf)) counter_1 (
    .load(Load), .D(subtractor_1_out), .count(Count), .Q(counter_1_q), .clk(CLK), .clr(or_3_out));  // open: carry
  or or_3 (or_3_out, ~Chip_Select, Reset);  // OR_Gate
  Comparator #(.width(4), .mode("unsigned")) comparator_1 (
    .a(4'b0000), .b(counter_1_q), .eq(Zero_Time));  // open: gt, lt
  or or_4 (or_4_out, Count, Load0, Load1);
  Register #(.width(32)) register_1 (.D(Data_In_0), .en(Chip_Select), .Q(register_1_q), .clk(CLK), .clr(or_5_out));
  or or_5 (or_5_out, ~Chip_Select, Reset);  // OR_Gate
  Register #(.width(32)) register_2 (.D(Data_In_1), .en(Chip_Select), .Q(register_2_q), .clk(CLK), .clr(or_6_out));
  or or_6 (or_6_out, ~Chip_Select, Reset);  // OR_Gate
  Register #(.width(32)) register_3 (.D(Data_In_2), .en(Chip_Select), .Q(register_3_q), .clk(CLK), .clr(or_7_out));
  or or_7 (or_7_out, ~Chip_Select, Reset);  // OR_Gate
  Register #(.width(32)) register_4 (.D(Data_In_3), .en(Chip_Select), .Q(register_4_q), .clk(CLK), .clr(or_8_out));
  or or_8 (or_8_out, ~Chip_Select, Reset);  // OR_Gate
  Register #(.width(32)) register_5 (
    .D({{11{1'b1}}, nRead_Write, Mask, Address}), .en(Chip_Select), .Q(register_5_q), .clk(CLK),
    .clr(or_9_out));
  or or_9 (or_9_out, ~Chip_Select, Reset);  // OR_Gate
  D_Flip_Flop Proc (.clk(CLK), .D(or_4_out), .Q(Proc_q), .reset(or_10_out));  // open: Qn, preset, en
  or or_10 (or_10_out, ~Chip_Select, Reset);  // OR_Gate
  Demultiplexer #(.enable("false")) demultiplexer_2 (
    .out0(Count), .out1(Update_Mem), .in(demultiplexer_3_out0), .sel(Zero_Time));
  Demultiplexer #(.enable("false")) demultiplexer_3 (
    .out0(demultiplexer_3_out0), .out1(Load1), .in(Proc_q), .sel(Changed));
  Clock clock_1 (.out(CLK));
  Comparator #(.width(32)) comparator_2 (.a(register_1_q), .b(Data_In_0), .eq(comparator_2_eq));  // open: gt, lt
  Comparator #(.width(32)) comparator_3 (.a(register_2_q), .b(Data_In_1), .eq(comparator_3_eq));  // open: gt, lt
  Comparator #(.width(32)) comparator_4 (.a(register_3_q), .b(Data_In_2), .eq(comparator_4_eq));  // open: gt, lt
  Comparator #(.width(32)) comparator_5 (.a(register_4_q), .b(Data_In_3), .eq(comparator_5_eq));  // open: gt, lt
  Comparator #(.width(32)) comparator_6 (
    .a(register_5_q), .b({{11{1'b1}}, nRead_Write, Mask, Address}), .eq(comparator_6_eq));  // open: gt, lt
  nand nand_1 (nand_1_out, comparator_6_eq, comparator_2_eq, comparator_3_eq, comparator_4_eq, comparator_5_eq);
  and and_1 (Changed, nand_1_out, Chip_Select);
  or or_11 (Load, Count, Load1, Load0);
  and and_2 (and_2_out, Mask[0], Update_Mem, nRead_Write);
  and and_3 (and_3_out, Mask[1], Update_Mem, nRead_Write);
  and and_4 (and_4_out, Mask[2], Update_Mem, nRead_Write);
  and and_5 (and_5_out, Mask[3], Update_Mem, nRead_Write);
  RAM_part #(.addrWidth(16), .dataWidth(32), .bus("separate")) ram_1 (
    .addr(Address), .din(Data_In_0), .data(Data_Out_0), .str(and_2_out), .sel(Chip_Select), .clk(CLK),
    .ld(and_6_out), .clr(Reset));
  and and_6 (and_6_out, ~nRead_Write, Idle);  // AND_Gate
  RAM_part #(.addrWidth(16), .dataWidth(32), .bus("separate")) ram_2 (
    .addr(Address), .din(Data_In_1), .data(Data_Out_1), .str(and_3_out), .sel(Chip_Select), .clk(CLK),
    .ld(and_7_out), .clr(Reset));
  and and_7 (and_7_out, ~nRead_Write, Idle);  // AND_Gate
  RAM_part #(.addrWidth(16), .dataWidth(32), .bus("separate")) ram_3 (
    .addr(Address), .din(Data_In_2), .data(Data_Out_2), .str(and_4_out), .sel(Chip_Select), .clk(CLK),
    .ld(and_8_out), .clr(Reset));
  and and_8 (and_8_out, ~nRead_Write, Idle);  // AND_Gate
  RAM_part #(.addrWidth(16), .dataWidth(32), .bus("separate")) ram_4 (
    .addr(Address), .din(Data_In_3), .data(Data_Out_3), .str(and_5_out), .sel(Chip_Select), .clk(CLK),
    .ld(and_9_out), .clr(Reset));
  and and_9 (and_9_out, ~nRead_Write, Idle);  // AND_Gate

  assign Read_Time = 4'b0011;
  assign Write_Time = 4'b0010;

  // Other names for the same wires on the sheet: M0 = Mask[0]; M1 = Mask[1]; M2 = Mask[2]; M3 = Mask[3];
  //   RW = nRead_Write; CLR = Reset; CS = Chip_Select; Load2 = Count

  // Notes on the sheet:
  //   NO MODIFICAR
  //   excepto quizás los valores RT y WT
  //   BANK0
  //   BANK1
  //   BANK2
  //   BANK3
endmodule

module S_MIPS (
  input  Kbd_Available,
  input  [6:0] Kbd_ASCII_Data,
  input  [31:0] RAM_Out_0,
  input  [31:0] RAM_Out_1,
  input  Reset,
  input  [31:0] RAM_Out_2,
  input  Clock,
  input  [31:0] RAM_Out_3,
  input  [3:0] Read_Time,
  input  [3:0] Write_Time,
  output Kbd_Enable,
  output [15:0] Address,
  output Kbd_Clear,
  output TTY_Enable,
  output [6:0] TTY_ASCII_Data,
  output Stop,
  output [31:0] RAM_In_0,
  output [31:0] RAM_In_1,
  output [31:0] RAM_In_2,
  output [31:0] RAM_In_3,
  output [3:0] Mask,
  output nRead_Write,
  output Chip_Select
);


  // Other names for the same wires on the sheet: CLK = Clock; CLR = Reset; CS = Chip_Select;
  //   KBD_AVAIL = Kbd_Available; KBD_CLR = Kbd_Clear; KBD_DATA[6:0] = Kbd_ASCII_Data; RAM_A[15:0] = Address;
  //   RAM_INPUT_0[31:0] = RAM_In_0; RAM_INPUT_1[31:0] = RAM_In_1; RAM_INPUT_2[31:0] = RAM_In_2;
  //   RAM_INPUT_3[31:0] = RAM_In_3; RAM_MASK[3:0] = Mask; RAM_OUTPUT_0[31:0] = RAM_Out_0;
  //   RAM_OUTPUT_1[31:0] = RAM_Out_1; RAM_OUTPUT_2[31:0] = RAM_Out_2; RAM_OUTPUT_3[31:0] = RAM_Out_3;
  //   RW = nRead_Write; TTY_DATA[6:0] = TTY_ASCII_Data

  // Notes on the sheet:
  //   RAM ADDRESS
  //   DATA FROM RAM
  //   DATA TO RAM
  //   DATA WRITE MASK
  //   RAM TIMING
  //   RAM CONTROL
  //   KEYBOARD
  //   TTY
  //   SEQUENCING
endmodule

module RAM_Dispatcher (
  input  [3:0] WriteTime,
  input  Clock,
  input  CLR,
  output [31:0] Data,
  output [15:0] Address,
  output [3:0] Mask,
  output Finished,
  output Write
);

  wire demultiplexer_2_out1, demultiplexer_3_out1, End, IDLE_q, IncAddr, Load, or_1_out, or_2_out, While_q,
       WriteEnd;
  wire [3:0] counter_1_q;
  wire [31:0] CurrentAddress_q;

  Counter #(.width(32), .max('hffffffff)) CurrentAddress (
    .count(IncAddr), .Q({CurrentAddress_q[31:18], Address, CurrentAddress_q[1:0]}), .clk(Clock), .clr(CLR));  // open: load, D, carry
  or or_1 (or_1_out, IncAddr, demultiplexer_3_out1, Finished);
  D_Flip_Flop IDLE (.clk(Clock), .D(or_1_out), .Q(IDLE_q), .preset(CLR));  // open: Qn, en, reset
  Demultiplexer #(.enable("false")) demultiplexer_1 (.out0(Load), .out1(Finished), .in(IDLE_q), .sel(End));
  D_Flip_Flop While (.clk(Clock), .D(or_2_out), .Q(While_q), .reset(CLR));  // open: Qn, preset, en
  or or_2 (or_2_out, Write, Load);
  RAM_part #(.addrWidth(18), .dataWidth(32)) ram_1 (
    .addr({Address, CurrentAddress_q[1:0]}), .data(Data), .clk(Clock));  // open: sel, ld, clr
  Demultiplexer #(.enable("false")) demultiplexer_2 (
    .out0(Write), .out1(demultiplexer_2_out1), .in(While_q), .sel(WriteEnd));
  Decoder #(.select(2)) decoder_1 (
    .out0(Mask[0]), .out1(Mask[1]), .out2(Mask[2]), .out3(Mask[3]), .sel(CurrentAddress_q[1:0]));  // open: en
  Demultiplexer #(.enable("false")) demultiplexer_3 (
    .out0(IncAddr), .out1(demultiplexer_3_out1), .in(demultiplexer_2_out1), .sel(End));
  Counter #(.width(4), .max('hf)) counter_1 (
    .load(Load), .D(WriteTime), .count(Write), .Q(counter_1_q), .clk(Clock));  // open: carry, clr
  Comparator #(.width(32)) comparator_1 (.a(Data), .b({32{1'b1}}), .eq(End));  // open: gt, lt
  Comparator #(.width(4)) comparator_2 (.a(4'b0000), .b(counter_1_q), .eq(WriteEnd));  // open: gt, lt

  // Other names for the same wires on the sheet: CLK = Clock; Count = Write; WT[3:0] = WriteTime
endmodule

module Multiplier (
  input  [31:0] A,
  input  [31:0] B,
  input  Signed,
  output [31:0] Hi,
  output [31:0] Lo
);

  wire adder_1_cout, adder_3_cout, adder_5_cout, and_1_out;
  wire [31:0] adder_1_out, adder_2_out, adder_3_out, adder_4_out, Hi_S, Hi_U, Lo_S, Lo_U, mux32b_x2_3_output,
       mux32b_x2_4_output, X, Y;

  Multiplier_part #(.width(32)) multiplier_1 (.a(X), .b(Y), .out(Lo_S), .cout(Hi_S));  // open: cin
  MUX32b_x2 mux32b_x2_1 (.Input1({1'b0, A[31:1]}), .Input2(A), .Selector(Signed), .Output(X));
  MUX32b_x2 mux32b_x2_2 (.Input1({1'b0, B[31:1]}), .Input2(B), .Selector(Signed), .Output(Y));
  MUX32b_x2 mux32b_x2_3 (.Input1({32{1'b0}}), .Input2({B[31:1], 1'b0}), .Selector(A[0]), .Output(mux32b_x2_3_output));
  Adder #(.width(32)) adder_1 (
    .a({Lo_S[29:0], 2'b00}), .b(mux32b_x2_3_output), .out(adder_1_out), .cout(adder_1_cout));  // open: cin
  Adder #(.width(32)) adder_2 (
    .a({32{1'b0}}), .b({Hi_S[29:0], Lo_S[31:30]}), .out(adder_2_out), .cin(adder_1_cout));  // open: cout
  MUX32b_x2 mux32b_x2_4 (.Input1({32{1'b0}}), .Input2({A[31:1], 1'b0}), .Selector(B[0]), .Output(mux32b_x2_4_output));
  Adder #(.width(32)) adder_3 (
    .a(adder_1_out), .b(mux32b_x2_4_output), .out(adder_3_out), .cout(adder_3_cout));  // open: cin
  Adder #(.width(32)) adder_4 (.a(adder_2_out), .b({32{1'b0}}), .out(adder_4_out), .cin(adder_3_cout));  // open: cout
  MUX32b_x2 mux32b_x2_5 (.Input1(Hi_U), .Input2(Hi_S), .Selector(Signed), .Output(Hi));
  MUX32b_x2 mux32b_x2_6 (.Input1(Lo_U), .Input2(Lo_S), .Selector(Signed), .Output(Lo));
  and and_1 (and_1_out, A[0], B[0]);
  Adder #(.width(32)) adder_5 (.a({32{1'b0}}), .b(adder_3_out), .out(Lo_U), .cin(and_1_out), .cout(adder_5_cout));
  Adder #(.width(32)) adder_6 (.a(adder_4_out), .b({32{1'b0}}), .out(Hi_U), .cin(adder_5_cout));  // open: cout

  // Other names for the same wires on the sheet: S = Signed; shl_A[30:0] = A[31:1]; shr_A[31:1] = A[31:1];
  //   shl_B[30:0] = B[31:1]; shr_B[31:1] = B[31:1]

  // Notes on the sheet:
  //   Multiplier
endmodule

module MUX32b_x2 (
  input  [31:0] Input1,
  input  [31:0] Input2,
  input  Selector,
  output [31:0] Output
);

  wire decoder_1_out0, decoder_1_out1;

  Decoder decoder_1 (.out0(decoder_1_out0), .out1(decoder_1_out1), .sel(Selector));  // open: en
  Transistor #(.\type ("n"), .gate("br"), .width(32)) transistor_1 (.in(Input1), .out(Output), .gate(decoder_1_out0));
  Transistor #(.\type ("n"), .gate("br"), .width(32)) transistor_2 (.in(Input2), .out(Output), .gate(decoder_1_out1));
endmodule

module Divider (
  input  [31:0] A,
  input  [31:0] B,
  input  Signed,
  output [31:0] R,
  output [31:0] C
);

  wire A_Sel, B_Sel, Out_Sel;
  wire [31:0] C_t, minus_A, minus_B, minus_C, minus_R, R_t, X, Y;

  and and_1 (A_Sel, Signed, A[31]);
  and and_2 (B_Sel, Signed, B[31]);
  xor xor_1 (Out_Sel, A_Sel, B_Sel);
  Negator #(.width(32)) negator_1 (.in(A), .out(minus_A));
  Negator #(.width(32)) negator_2 (.in(B), .out(minus_B));
  MUX32b_x2 mux32b_x2_1 (.Input1(C_t), .Input2(minus_C), .Selector(Out_Sel), .Output(C));
  Divider_part #(.width(32)) divider_1 (.a(X), .b(Y), .out(C_t), .rem(R_t));  // open: upper
  MUX32b_x2 mux32b_x2_2 (.Input1(R_t), .Input2(minus_R), .Selector(Out_Sel), .Output(R));
  MUX32b_x2 mux32b_x2_3 (.Input1(A), .Input2(minus_A), .Selector(A_Sel), .Output(X));
  Negator #(.width(32)) negator_3 (.in(R_t), .out(minus_R));
  MUX32b_x2 mux32b_x2_4 (.Input1(B), .Input2(minus_B), .Selector(B_Sel), .Output(Y));
  Negator #(.width(32)) negator_4 (.in(C_t), .out(minus_C));

  // Other names for the same wires on the sheet: A_Sg = A[31]; B_Sg = B[31]; S = Signed

  // Notes on the sheet:
  //   Divider
endmodule

module ALU (
  input  [31:0] A,
  input  [31:0] B,
  input  [5:0] in_FuncCode,
  input  CLK,
  input  RST,
  output [31:0] Output,
  output [31:0] Hi,
  output [31:0] Low,
  output N,
  output Z
);

  wire and_2_out, comparator_1_eq, comparator_1_gt, comparator_1_lt, comparator_2_gt, comparator_2_lt, div,
       divu, en_Hi, mult, mult_o_mulu, mulu, mulu_o_divu, not_1_out, selector2_1_output, Z1, Z2;
  wire [3:0] FuncCode;
  wire [31:0] A_and_B, A_B, A_B_Hi, A_B_Hi_t, A_B_Lo, A_B_Lo_t, A_B_signed, A_B_signed_t, A_B_t, A_B_t_t,
       A_B_unsigned, A_B_unsigned_t, A_nor_B, A_or_B, A_xor_B, mux32b_x2_1_output, mux32b_x2_2_output;

  Selector3 selector3_1 (
    .Input5(in_FuncCode[5]), .Input4(in_FuncCode[4]), .Input3(in_FuncCode[3]), .Input2(in_FuncCode[2]),
    .Input1(in_FuncCode[1]), .Input0(in_FuncCode[0]), .Output3(FuncCode[3]), .Output2(FuncCode[2]),
    .Output1(FuncCode[1]), .Output0(FuncCode[0]));
  Selector2 selector2_1 (
    .input1(in_FuncCode[5]), .input2(in_FuncCode[4]), .input3(in_FuncCode[3]), .input4(in_FuncCode[2]),
    .input5(in_FuncCode[1]), .input6(in_FuncCode[0]), .\output (selector2_1_output));
  EqualityComparer6bits equalitycomparer6bits_1 (.in_1(in_FuncCode), .in_2(6'b011000), .out_3(mult));
  EqualityComparer6bits equalitycomparer6bits_2 (.in_1(in_FuncCode), .in_2(6'b011001), .out_3(mulu));
  EqualityComparer6bits equalitycomparer6bits_3 (.in_1(in_FuncCode), .in_2(6'b011011), .out_3(divu));
  EqualityComparer6bits equalitycomparer6bits_4 (.in_1(in_FuncCode), .in_2(6'b011010), .out_3(div));
  MUX32b_x16 mux32b_x16_1 (
    .in_1(A_B), .in_2(A_B_signed), .in_3(A_B_unsigned), .in_4(A_and_B), .in_5(A_or_B), .in_6(A_xor_B),
    .in_7(A_B_Hi_t), .in_8(A_B_Lo_t), .in_9(A_B_t), .in_10(A_nor_B), .in_17(FuncCode), .out_18(Output));  // open: in_11, in_12, in_13, in_14, in_15, in_16
  MUX32b_x2 mux32b_x2_1 (
    .Input1(A_B_Hi_t), .Input2(A_B_Hi), .Selector(selector2_1_output), .Output(mux32b_x2_1_output));
  MUX32b_x2 mux32b_x2_2 (
    .Input1(A_B_Lo), .Input2(A_B_Lo_t), .Selector(selector2_1_output), .Output(mux32b_x2_2_output));
  Adder #(.width(32)) adder_1 (.a(A), .b(B), .out(A_B));  // open: cin, cout
  Subtractor #(.width(32)) subtractor_1 (.a(A), .b(B), .out(A_B_t));  // open: bin, bout
  Multiplier multiplier_1 (.A(A), .B(B), .Signed(mult), .Hi(A_B_Hi_t), .Lo(A_B_Lo));
  Divider divider_1 (.A(A), .B(B), .Signed(div), .R(A_B_Lo_t), .C(A_B_Hi));
  Register #(.width(32)) u_Hi (.D(mux32b_x2_1_output), .en(en_Hi), .Q(Hi), .clk(CLK), .clr(RST));
  Register #(.width(32)) u_Low (.D(mux32b_x2_2_output), .en(en_Hi), .Q(Low), .clk(CLK), .clr(RST));
  or or_1 (mult_o_mulu, mult, mulu);
  or or_2 (mulu_o_divu, mulu, divu);
  assign A_and_B = A & B;  // AND_Gate and_1, 32 bits wide
  assign A_or_B = A | B;  // OR_Gate or_3, 32 bits wide
  assign A_nor_B = ~(A | B);  // NOR_Gate nor_1, 32 bits wide
  assign A_xor_B = A ^ B;  // XOR_Gate xor_1, 32 bits wide
  nor nor_2 (Z1, Output[31], Output[30], Output[29], Output[28], Output[27], Output[26], Output[25], Output[24], Output[23], Output[22], Output[21], Output[20], Output[19], Output[18], Output[17], Output[16], Output[15], Output[14], Output[13], Output[12], Output[11], Output[10], Output[9], Output[8], Output[7], Output[6], Output[5], Output[4], Output[3], Output[2], Output[1], Output[0]);
  or or_4 (en_Hi, mult_o_mulu, mulu_o_divu, div);
  Comparator #(.width(32)) comparator_1 (
    .a(A), .b(B), .gt(comparator_1_gt), .eq(comparator_1_eq), .lt(comparator_1_lt));
  Comparator #(.width(32), .mode("unsigned")) comparator_2 (
    .a(A), .b(B), .gt(comparator_2_gt), .lt(comparator_2_lt));  // open: eq
  not not_1 (not_1_out, mulu_o_divu);
  and and_2 (and_2_out, Z1, Z2);
  BitExtensor_1To32 bitextensor_1to32_1 (.N(comparator_1_gt), .Input(1'b0), .Output(A_B_signed_t));
  BitExtensor_1To32 bitextensor_1to32_2 (.N(comparator_1_eq), .Input(1'b0), .Output(A_B_t_t));
  BitExtensor_1To32 bitextensor_1to32_3 (.N(comparator_1_lt), .Input(1'b0), .Output(A_B_signed));
  BitExtensor_1To32 bitextensor_1to32_4 (.N(comparator_2_gt), .Input(1'b0), .Output(A_B_unsigned_t));
  BitExtensor_1To32 bitextensor_1to32_5 (.N(comparator_2_lt), .Input(1'b0), .Output(A_B_unsigned));
  and and_3 (N, Output[31], not_1_out);
  MUX01b_x2 mux01b_x2_1 (.Input1(Z1), .Input2(and_2_out), .Selector(mult_o_mulu), .Output(Z));
  nor nor_3 (Z2, Low[31], Low[30], Low[29], Low[28], Low[27], Low[26], Low[25], Low[24], Low[23], Low[22], Low[21], Low[20], Low[19], Low[18], Low[17], Low[16], Low[15], Low[14], Low[13], Low[12], Low[11], Low[10], Low[9], Low[8], Low[7], Low[6], Low[5], Low[4], Low[3], Low[2], Low[1], Low[0]);

  // Other names for the same wires on the sheet: en_Lo = en_Hi; N1 = Output[31]

  // Notes on the sheet:
  //   Signed comparison
  //   Unsigned comparison
endmodule

module EqualityComparer6bits (
  input  [5:0] in_1,
  input  [5:0] in_2,
  output out_3
);

  wire xor_1_out, xor_2_out, xor_3_out, xor_4_out, xor_5_out, xor_6_out;

  xor xor_1 (xor_1_out, in_1[0], in_2[0]);
  xor xor_2 (xor_2_out, in_1[1], in_2[1]);
  xor xor_3 (xor_3_out, in_1[2], in_2[2]);
  xor xor_4 (xor_4_out, in_1[3], in_2[3]);
  xor xor_5 (xor_5_out, in_1[4], in_2[4]);
  xor xor_6 (xor_6_out, in_1[5], in_2[5]);
  nor nor_1 (out_3, xor_1_out, xor_2_out, xor_3_out, xor_4_out, xor_5_out, xor_6_out);

  // Other names for the same wires on the sheet: InA0 = in_1[0]; InA1 = in_1[1]; InA2 = in_1[2]; InA3 = in_1[3];
  //   InA4 = in_1[4]; InA5 = in_1[5]; InB0 = in_2[0]; InB1 = in_2[1]; InB2 = in_2[2]; InB3 = in_2[3]; InB4 = in_2[4];
  //   InB5 = in_2[5]
endmodule

module MUX01b_x2 (
  input  Input1,
  input  Input2,
  input  Selector,
  output Output
);

  wire decoder_1_out0, decoder_1_out1;

  Decoder decoder_1 (.out0(decoder_1_out0), .out1(decoder_1_out1), .sel(Selector));  // open: en
  Transistor #(.\type ("n"), .gate("br")) transistor_1 (.in(Input1), .out(Output), .gate(decoder_1_out0));
  Transistor #(.\type ("n"), .gate("br")) transistor_2 (.in(Input2), .out(Output), .gate(decoder_1_out1));
endmodule

module BitExtensor_1To32 (
  input  N,
  input  Input,
  output [31:0] Output
);


  assign Output = {{31{Input}}, N};
endmodule

module Selector (
  input  input1,
  input  input2,
  input  input3,
  output \output ,
  output output1
);

  wire not_1_out, not_2_out;

  not not_1 (not_1_out, input1);
  not not_2 (not_2_out, input2);
  and and_1 (\output , not_1_out, input2);
  and and_2 (output1, not_2_out, input3);
endmodule

module Selector1 (
  input  input1,
  input  input2,
  input  input3,
  input  input4,
  input  input5,
  input  input6,
  output output1,
  output output2,
  output output3
);

  wire and_1_out, and_2_out, and_3_out, and_4_out, and_5_out, and_6_out, and_7_out, and_8_out, and_9_out,
       not_1_out, not_2_out, not_3_out, not_4_out, not_5_out, not_6_out, not_7_out, not_8_out, not_9_out;

  not not_1 (not_1_out, input3);
  not not_2 (not_2_out, input5);
  not not_3 (not_3_out, input6);
  not not_4 (not_4_out, input4);
  not not_5 (not_5_out, input4);
  not not_6 (not_6_out, input5);
  not not_7 (not_7_out, input1);
  not not_8 (not_8_out, input6);
  not not_9 (not_9_out, input6);
  and and_1 (and_1_out, not_1_out, input5);
  and and_2 (and_2_out, input4, input6);
  and and_3 (and_3_out, input4, input5);
  and and_4 (and_4_out, input5, input6);
  and and_5 (and_5_out, input4, not_2_out, not_3_out);
  and and_6 (and_6_out, input1, not_4_out, input5);
  and and_7 (and_7_out, not_5_out, not_6_out, input6);
  and and_8 (and_8_out, not_7_out, input5, not_8_out);
  and and_9 (and_9_out, input4, not_9_out);
  or or_1 (output1, and_1_out, and_2_out, and_3_out);
  or or_2 (output2, and_4_out, and_5_out, and_6_out);
  or or_3 (output3, and_7_out, and_8_out, and_9_out);
endmodule

module Selector2 (
  input  input1,
  input  input2,
  input  input3,
  input  input4,
  input  input5,
  input  input6,
  output \output 
);


  assign \output  = input5;
endmodule

module Selector3 (
  input  Input5,
  input  Input4,
  input  Input3,
  input  Input2,
  input  Input1,
  input  Input0,
  output Output3,
  output Output2,
  output Output1,
  output Output0
);

  wire and_1_out, and_2_out, and_3_out, and_4_out, and_5_out, and_6_out, and_7_out, and_8_out, and_9_out,
       and_10_out, and_11_out, and_12_out, not_1_out, not_2_out, not_3_out, not_4_out, not_5_out, not_6_out,
       not_7_out, not_8_out, not_9_out, not_10_out, not_11_out, not_12_out, not_13_out, not_14_out,
       not_15_out, not_16_out;

  not not_1 (not_1_out, Input3);
  not not_2 (not_2_out, Input0);
  not not_3 (not_3_out, Input4);
  not not_4 (not_4_out, Input3);
  not not_5 (not_5_out, Input1);
  not not_6 (not_6_out, Input5);
  not not_7 (not_7_out, Input2);
  not not_8 (not_8_out, Input1);
  not not_9 (not_9_out, Input0);
  not not_10 (not_10_out, Input2);
  not not_11 (not_11_out, Input1);
  not not_12 (not_12_out, Input0);
  not not_13 (not_13_out, Input0);
  not not_14 (not_14_out, Input0);
  not not_15 (not_15_out, Input4);
  not not_16 (not_16_out, Input0);
  and and_1 (and_1_out, not_1_out, Input1, not_2_out);
  and and_2 (and_2_out, Input5, not_3_out, not_4_out, Input2, Input1);
  and and_3 (and_3_out, Input2, not_5_out, Input0);
  and and_4 (and_4_out, not_6_out, Input2, Input1);
  and and_5 (and_5_out, Input3, Input2, Input0);
  and and_6 (and_6_out, Input5, Input3, not_7_out, not_8_out, not_9_out);
  and and_7 (and_7_out, not_10_out, Input0);
  and and_8 (and_8_out, Input2, not_11_out, not_12_out);
  and and_9 (and_9_out, Input2, not_13_out);
  and and_10 (and_10_out, Input2, Input1);
  and and_11 (and_11_out, Input3, Input1, not_14_out);
  and and_12 (and_12_out, Input5, not_15_out, Input3, not_16_out);
  or or_1 (Output3, and_1_out, and_2_out);
  or or_2 (Output2, and_3_out, and_4_out, and_5_out, Input4, and_6_out);
  or or_3 (Output1, and_7_out, and_8_out, Input4);
  or or_4 (Output0, and_9_out, and_10_out, and_11_out, and_12_out);
endmodule

module MUX32b_x16 (
  input  [31:0] in_1,
  input  [31:0] in_2,
  input  [31:0] in_3,
  input  [31:0] in_4,
  input  [31:0] in_5,
  input  [31:0] in_6,
  input  [31:0] in_7,
  input  [31:0] in_8,
  input  [31:0] in_9,
  input  [31:0] in_10,
  input  [31:0] in_11,
  input  [31:0] in_12,
  input  [31:0] in_13,
  input  [31:0] in_14,
  input  [31:0] in_15,
  input  [31:0] in_16,
  input  [3:0] in_17,
  output [31:0] out_18
);

  wire decoder_1_out0, decoder_1_out1, decoder_1_out2, decoder_1_out3, decoder_1_out4, decoder_1_out5,
       decoder_1_out6, decoder_1_out7, decoder_1_out8, decoder_1_out9, decoder_1_out10, decoder_1_out11,
       decoder_1_out12, decoder_1_out13, decoder_1_out14, decoder_1_out15;

  Transistor #(.\type ("n"), .gate("br"), .width(32)) transistor_1 (.in(in_1), .out(out_18), .gate(decoder_1_out0));
  Transistor #(.\type ("n"), .gate("br"), .width(32)) transistor_2 (.in(in_2), .out(out_18), .gate(decoder_1_out1));
  Decoder #(.select(4), .enable("false")) decoder_1 (
    .out0(decoder_1_out0), .out1(decoder_1_out1), .out2(decoder_1_out2), .out3(decoder_1_out3),
    .out4(decoder_1_out4), .out5(decoder_1_out5), .out6(decoder_1_out6), .out7(decoder_1_out7),
    .out8(decoder_1_out8), .out9(decoder_1_out9), .out10(decoder_1_out10), .out11(decoder_1_out11),
    .out12(decoder_1_out12), .out13(decoder_1_out13), .out14(decoder_1_out14), .out15(decoder_1_out15),
    .sel(in_17));
  Transistor #(.\type ("n"), .gate("br"), .width(32)) transistor_3 (.in(in_3), .out(out_18), .gate(decoder_1_out2));
  Transistor #(.\type ("n"), .gate("br"), .width(32)) transistor_4 (.in(in_4), .out(out_18), .gate(decoder_1_out3));
  Transistor #(.\type ("n"), .gate("br"), .width(32)) transistor_5 (.in(in_5), .out(out_18), .gate(decoder_1_out4));
  Transistor #(.\type ("n"), .gate("br"), .width(32)) transistor_6 (.in(in_6), .out(out_18), .gate(decoder_1_out5));
  Transistor #(.\type ("n"), .gate("br"), .width(32)) transistor_7 (.in(in_7), .out(out_18), .gate(decoder_1_out6));
  Transistor #(.\type ("n"), .gate("br"), .width(32)) transistor_8 (.in(in_8), .out(out_18), .gate(decoder_1_out7));
  Transistor #(.\type ("n"), .gate("br"), .width(32)) transistor_9 (.in(in_9), .out(out_18), .gate(decoder_1_out8));
  Transistor #(.\type ("n"), .gate("br"), .width(32)) transistor_10 (.in(in_10), .out(out_18), .gate(decoder_1_out9));
  Transistor #(.\type ("n"), .gate("br"), .width(32)) transistor_11 (.in(in_11), .out(out_18), .gate(decoder_1_out10));
  Transistor #(.\type ("n"), .gate("br"), .width(32)) transistor_12 (.in(in_12), .out(out_18), .gate(decoder_1_out11));
  Transistor #(.\type ("n"), .gate("br"), .width(32)) transistor_13 (.in(in_13), .out(out_18), .gate(decoder_1_out12));
  Transistor #(.\type ("n"), .gate("br"), .width(32)) transistor_14 (.in(in_14), .out(out_18), .gate(decoder_1_out13));
  Transistor #(.\type ("n"), .gate("br"), .width(32)) transistor_15 (.in(in_15), .out(out_18), .gate(decoder_1_out14));
  Transistor #(.\type ("n"), .gate("br"), .width(32)) transistor_16 (.in(in_16), .out(out_18), .gate(decoder_1_out15));
endmodule
